// Logisim project lab2.circ as structural Verilog: 1 circuit, main circuit main
module main (
  input  A,
  input  B,
  output out_3,
  output S
);

  wire and_1_out, and_2_out, not_1_out, not_2_out;

  not not_1 (not_1_out, A);
  not not_2 (not_2_out, B);
  and and_1 (and_1_out, not_1_out, not_1_out, B, B);
  and and_2 (and_2_out, A, not_2_out, not_2_out);
  or or_1 (S, and_1_out, and_1_out, and_2_out, and_2_out);
  and and_3 (out_3, A, B);
endmodule
