// Logisim project Lab3.circ as structural Verilog: 1 circuit, main circuit main
module main (
  input  b_in,
  input  B,
  input  A,
  input  in_4,
  output out_5,
  output b_out
);

  wire and_1_out, and_2_out, xor_1_out, xor_2_out, xor_3_out;

  xor xor_1 (xor_1_out, b_in, B);
  xor xor_2 (xor_2_out, A, in_4);
  xor xor_3 (xor_3_out, b_in, B);
  and and_1 (and_1_out, B, b_in);
  and and_2 (and_2_out, xor_1_out, xor_2_out);
  xor xor_4 (out_5, xor_3_out, A);
  or or_1 (b_out, and_1_out, and_2_out);
endmodule
