// Logisim project lab4.circ as structural Verilog: 1 circuit, main circuit main
module main (
  input  A,
  input  B,
  input  C,
  input  D,
  output E,
  output G,
  output L
);

  wire and_1_out, and_2_out, and_4_out, not_1_out, not_2_out, not_3_out, not_4_out, xnor_1_out, xnor_2_out;

  xnor xnor_1 (xnor_1_out, A, C);
  xnor xnor_2 (xnor_2_out, B, D);
  not not_1 (not_1_out, B);
  not not_2 (not_2_out, A);
  and and_1 (and_1_out, not_2_out, C);
  and and_2 (and_2_out, not_1_out, D, C);
  and and_3 (E, xnor_1_out, xnor_2_out);
  and and_4 (and_4_out, not_1_out, D, not_2_out);
  or or_1 (L, and_4_out, and_4_out, and_1_out, and_2_out);
  not not_3 (not_3_out, E);
  not not_4 (not_4_out, L);
  and and_5 (G, not_3_out, not_4_out);
endmodule
