// Logisim project lab4v2.circ as structural Verilog: 1 circuit, main circuit main
module main (
  input  in_1,
  input  in_2,
  input  in_3,
  input  in_4,
  input  in_5,
  output out_6,
  output out_7,
  output out_8
);

  wire nand_1_out, nand_2_out, nand_3_out, nand_5_out, nand_6_out, not_1_out, not_2_out, not_3_out,
       not_4_out, not_5_out, not_6_out;

  not not_1 (not_1_out, in_2);
  not not_2 (not_2_out, in_4);
  nand nand_1 (nand_1_out, in_1, not_2_out);
  not not_3 (not_3_out, in_1);
  not not_4 (not_4_out, in_5);
  nand nand_2 (nand_2_out, not_1_out, nand_1_out, in_5);
  nand nand_3 (nand_3_out, not_3_out, in_4);
  nand nand_4 (out_6, nand_3_out, nand_2_out);
  nand nand_5 (nand_5_out, not_2_out, in_1);
  nand nand_6 (nand_6_out, nand_3_out, in_2, not_4_out);
  nand nand_7 (out_8, nand_5_out, nand_6_out);
  not not_5 (not_5_out, out_6);
  not not_6 (not_6_out, out_8);
  and and_1 (out_7, in_3, not_5_out, not_6_out);
endmodule
