// Logisim project k.circ as structural Verilog: 1 circuit, main circuit main
module main (
  input  in_1,
  input  in_2,
  input  in_3,
  input  in_4,
  input  in_5,
  input  in_6,
  input  in_7,
  input  in_8,
  output out_9,
  output out_10,
  output out_11,
  output out_12
);

  wire and_1_out, and_2_out, and_3_out, and_4_out;

  xor xor_1 (out_11, in_3, in_8);
  and and_1 (and_1_out, in_3, in_8);
  or or_1 (out_9, and_1_out, and_1_out);
  ExactlyOne xor_2 (.out(out_12), .in0(out_9), .in1(in_4), .in2(in_5));
  and and_2 (and_2_out, in_5, in_4);
  and and_3 (and_3_out, in_5, out_9);
  and and_4 (and_4_out, in_4, out_9);
  or or_2 (out_10, and_3_out, and_4_out, and_2_out);
endmodule
